# Fritzing sketch DuinoCoinI2C (saved by Fritzing 0.9.3b)

parts:
  Componente1 = Arduino Uno (Rev3)
  WeMos_D1_Mini1 = WeMos D1 Mini
  Componente2 = Arduino Uno (Rev3)
  Componente3 = Arduino Uno (Rev3)
  Componente4 = Arduino Uno (Rev3)

nets:
  N1: Componente1.A4/SDA, WeMos_D1_Mini1.D2, Componente2.A4/SDA, Componente3.A4/SDA, Componente4.A4/SDA
  N2: Componente1.A5/SCL, WeMos_D1_Mini1.D1, Componente2.A5/SCL, Componente3.A5/SCL, Componente4.A5/SCL
  5V: Componente1.5V, WeMos_D1_Mini1.3V3
  N3: Componente1.GND, WeMos_D1_Mini1.G
  5V_2: Componente2.5V, Componente3.5V
  GND: Componente2.GND, Componente3.GND

notes:
  3.3V
  Do not power the Arduino with the USB.
  Arduino is powered by 3.3V
  Warning!
